# Fritzing sketch traffic_light_crossover (saved by Fritzing 0.9.3b)
breadboards: 2

parts:
  MFRC522 = RFID-RC522-v2
  Red1 = smd LED [color="Red (633nm)" package="0603 [SMD]"]
  Yellow1 = smd LED [color="Yellow (585nm)" package="0603 [SMD]"]
  Green1 = smd LED [color="Green (570nm)" package="0603 [SMD]"]
  PedRed1 = smd LED [color="Red (633nm)" package="0603 [SMD]"]
  PedGreen1 = smd LED [color="Green (570nm)" package="0603 [SMD]"]
  Red2 = smd LED [color="Red (633nm)" package="0603 [SMD]"]
  Yellow2 = smd LED [color="Yellow (585nm)" package="0603 [SMD]"]
  Green2 = smd LED [color="Green (570nm)" package="0603 [SMD]"]
  PedRed2 = smd LED [color="Red (633nm)" package="0603 [SMD]"]
  PedGreen2 = smd LED [color="Green (570nm)" package="0603 [SMD]"]
  RTC = Real Time Clock Module - DS1307 RTC Breakout Board
  Buzzer = Piezo Speaker
  Arduino_Uno = Arduino Uno (Rev3) - ICSP

nets (from the breadboard view):
  N1: MFRC522.SDA, Arduino_Uno.D10_PWM/SS
  N2: MFRC522.SCK, Arduino_Uno.D13/SCK
  N3: MFRC522.MOSI, Arduino_Uno.ICSP_MOSI, Arduino_Uno.D11_PWM/MOSI
  N4: MFRC522.MISO, Arduino_Uno.D12/MISO
  GND: MFRC522.GND, Red1.cathode, Yellow1.cathode, Green1.cathode, PedRed1.cathode, PedGreen1.cathode, Red2.cathode, Yellow2.cathode, Green2.cathode, PedRed2.cathode, PedGreen2.cathode, RTC.GND, Buzzer.pin1, Arduino_Uno.GND
  N5: MFRC522.RST, Arduino_Uno.D9_PWM
  N6: MFRC522.3_3V, Arduino_Uno.3V3
  N7: Red1.anode, Arduino_Uno.D8
  N8: Yellow1.anode, Arduino_Uno.D7
  N9: Green1.anode, Arduino_Uno.D6_PWM
  N10: PedRed1.anode, Arduino_Uno.D5_PWM
  N11: PedGreen1.anode, Arduino_Uno.D4
  N12: Red2.anode, Arduino_Uno.D3_PWM
  N13: Yellow2.anode, Arduino_Uno.A3
  N14: Green2.anode, Arduino_Uno.A2
  N15: PedRed2.anode, Arduino_Uno.A1
  N16: PedGreen2.anode, Arduino_Uno.A0
  5V: RTC.5V, Arduino_Uno.5V
  N17: RTC.SCL, Arduino_Uno.A5/SCL
  N18: RTC.SDA, Arduino_Uno.A4/SDA
  N19: Buzzer.pin2, Arduino_Uno.D2

custom parts:
  RFID-RC522-v2: A simple China made RFID-RC522 Reader; do check the pin labels, as this is a MFRC522 based clone.
